# Fritzing sketch scheme (saved by Fritzing 0.9.6b)
breadboards: 1

parts:
  SOUND_METER = Breakout Board for Electret Microphone
  Part2 = Arduino Uno (Rev3) - ICSP
  Raspberry_Pi_1 = Raspberry Pi 3 [part_number=RPI-3-V1.2]  # not connected
  HIGH_SOUND_LED = LED - 5mm [color="Red (633nm)" current=0.030 package="5 mm [THT]"]
  R1 = Resistor [tolerance=±5% resistance=220 package="2512 [SMD]"]

nets:
  VCC: SOUND_METER.VCC, Part2.5V
  GND: SOUND_METER.GND, Part2.GND, R1.Pin_1
  N1: SOUND_METER.AUD, Part2.A0
  N2: Part2.D7, HIGH_SOUND_LED.anode
  N3: HIGH_SOUND_LED.cathode, R1.Pin_0
